# Fritzing sketch ColorLabSchematic (saved by Fritzing 0.8.7b)
breadboards: 1

parts:
  Part1 = Arduino Uno (Rev3)
  R1 = Resistor [tolerance=±5% resistance=100 package=THT]
  Q1 = Basic FET N-Channel [package="D2Pak [SMD]"]
  Q2 = Basic FET N-Channel [package="D2Pak [SMD]"]
  Q3 = Basic FET N-Channel [package="D2Pak [SMD]"]
  LED1 = LED - 5mm [color="Green (560nm)" current=20mA package="5 mm [THT]"]

nets:
  N1: Part1.D7, R1.Pin_0
  N2: Part1.5V, Q1.Gate, Q2.Gate, Q3.Gate, LED1.anode
  N3: Part1.GND, Q1.source, Q2.source, Q3.source
  N4: R1.Pin_1, LED1.cathode

notes:
  Analog LED Strip
  Parallax Serial RFID Reader
  R
  G
  B
  12V
  VCC
  /ENABLE
  SOUT
  GND
  12V DC Power Supply
